# Fritzing sketch 8x8_LED (saved by Fritzing 0.7.0b)
breadboards: 2

parts:
  Arduino1 = Arduino
  IC1 = DIP - 24 pins [package="DIP (Dual Inline) [THT]"]
  Part1 = LED Matrix - Serial Interface - Red/Green/Blue
  R1 = Rotary Potentiometer (Small) [maximum_resistance=100kΩ]
  R2 = Resistor [tolerance=±5% resistance=10 package=THT]
  R3 = Resistor [tolerance=±5% resistance=10 package=THT]
  R4 = Resistor [tolerance=±5% resistance=10 package=THT]

nets:
  N1: Arduino1.GND, IC1.pin4, IC1.pin9
  N2: Arduino1.D12, IC1.pin1
  N3: Arduino1.D11, IC1.pin13, IC1.pin14
  N4: Arduino1.D10, IC1.pin12
  N5: Arduino1.+5V, IC1.pin19, R3.Pin_1
  N6: Arduino1.A0, R1.wiper
  N7: IC1.pin7, Part1.CS
  N8: IC1.pin11, IC1.pin15, Part1.VCC
  N9: IC1.pin18, R2.Pin_0
  N10: IC1.pin20, Part1.GND
  N11: IC1.pin21, Part1.MOSI
  N12: IC1.pin22, Part1.SCK
  N13: R2.Pin_1, R4.Pin_0
  N14: R3.Pin_0, R4.Pin_1

custom parts:
  DIP - 24 pins: A DIP stand-in part for whatever IC you want. With 24 pins on a 300 mil dual inline package (DIP) footprint.
